# Fritzing sketch sketch (saved by Fritzing 0.9.5d)
perfboards: 1

parts:
  Part1 = Arduino Nano (Rev3.0) (ICSP)
  J1 = Screw terminal - 2 pins [package=THT]
  Squix1 = OLED 0.96" 128x64 I2C SSD1306
  J2 = Screw terminal - 2 pins [package=THT]

nets:
  N1: Part1.GND, J2.pin1
  N2: Part1.D11/MOSI, J1.pin1
  N3: Part1.D12/MISO, J1.pin2
  N4: Part1.VIN, J2.pin2
  N5: Part1.A5, Squix1.SCA
  N6: Part1.A4, Squix1.SCL
